// Logisim project DivisionBinaria.circ as structural Verilog: 20 circuits, main circuit main
module main (
  input  in_1,
  input  in_2,
  input  in_3,
  input  in_4,
  input  in_5,
  input  in_6,
  input  in_7,
  input  in_8,
  input  in_9
);

  wire d0_1_out_4, d0_2_out_4, display_de_7_segmentos_1_out_5, display_de_7_segmentos_1_out_6,
       display_de_7_segmentos_1_out_7, display_de_7_segmentos_1_out_8, display_de_7_segmentos_1_out_9,
       display_de_7_segmentos_1_out_10, display_de_7_segmentos_1_out_11, display_de_7_segmentos_2_out_5,
       display_de_7_segmentos_2_out_6, display_de_7_segmentos_2_out_7, display_de_7_segmentos_2_out_8,
       display_de_7_segmentos_2_out_9, display_de_7_segmentos_2_out_10, display_de_7_segmentos_2_out_11,
       display_de_7_segmentos_3_out_5, display_de_7_segmentos_3_out_6, display_de_7_segmentos_3_out_7,
       display_de_7_segmentos_3_out_8, display_de_7_segmentos_3_out_9, display_de_7_segmentos_3_out_10,
       display_de_7_segmentos_3_out_11, display_de_7_segmentos_4_out_5, display_de_7_segmentos_4_out_6,
       display_de_7_segmentos_4_out_7, display_de_7_segmentos_4_out_8, display_de_7_segmentos_4_out_9,
       display_de_7_segmentos_4_out_10, display_de_7_segmentos_4_out_11, display_especial_1_s,
       display_especial_1_u, display_especial_1_v, display_especial_1_w, display_especial_1_x,
       display_especial_1_y, display_especial_1_z, display_especial_de_0_1_s, display_especial_de_0_1_u,
       display_especial_de_0_1_v, display_especial_de_0_1_w, display_especial_de_0_1_x,
       display_especial_de_0_1_y, display_especial_de_0_1_z, pro_1_out_12, pro_1_out_13, pro_1_out_14,
       pro_1_out_15, pro_1_out_16, pro_1_out_17, pro_1_out_18, pro_1_out_19, pro_1_out_20;

  D0 d0_1 (.in_1(in_7), .in_2(in_8), .in_3(in_9), .out_4(d0_1_out_4));
  _7_Segment_Display u_7_segment_display_1 (
    .g(display_de_7_segmentos_1_out_11), .f(display_de_7_segmentos_1_out_10),
    .a(display_de_7_segmentos_1_out_5), .b(display_de_7_segmentos_1_out_6),
    .e(display_de_7_segmentos_1_out_9), .d(display_de_7_segmentos_1_out_8), .c(display_de_7_segmentos_1_out_7));  // open: dp
  Display_de_7_Segmentos display_de_7_segmentos_1 (
    .in_1(1'b0), .in_2(1'b0), .in_3(in_1), .in_4(in_2), .out_5(display_de_7_segmentos_1_out_5),
    .out_6(display_de_7_segmentos_1_out_6), .out_7(display_de_7_segmentos_1_out_7),
    .out_8(display_de_7_segmentos_1_out_8), .out_9(display_de_7_segmentos_1_out_9),
    .out_10(display_de_7_segmentos_1_out_10), .out_11(display_de_7_segmentos_1_out_11));
  _7_Segment_Display u_7_segment_display_2 (
    .g(display_de_7_segmentos_3_out_11), .f(display_de_7_segmentos_3_out_10),
    .a(display_de_7_segmentos_3_out_5), .b(display_de_7_segmentos_3_out_6),
    .e(display_de_7_segmentos_3_out_9), .d(display_de_7_segmentos_3_out_8), .c(display_de_7_segmentos_3_out_7));  // open: dp
  D0 d0_2 (.in_1(in_7), .in_2(in_8), .in_3(in_9), .out_4(d0_2_out_4));
  Display_de_7_Segmentos display_de_7_segmentos_2 (
    .in_1(1'b0), .in_2(in_7), .in_3(in_8), .in_4(in_9), .out_5(display_de_7_segmentos_2_out_5),
    .out_6(display_de_7_segmentos_2_out_6), .out_7(display_de_7_segmentos_2_out_7),
    .out_8(display_de_7_segmentos_2_out_8), .out_9(display_de_7_segmentos_2_out_9),
    .out_10(display_de_7_segmentos_2_out_10), .out_11(display_de_7_segmentos_2_out_11));
  _7_Segment_Display u_7_segment_display_3 (
    .g(display_de_7_segmentos_2_out_11), .f(display_de_7_segmentos_2_out_10),
    .a(display_de_7_segmentos_2_out_5), .b(display_de_7_segmentos_2_out_6),
    .e(display_de_7_segmentos_2_out_9), .d(display_de_7_segmentos_2_out_8), .c(display_de_7_segmentos_2_out_7));  // open: dp
  Pro pro_1 (
    .in_1(in_7), .in_2(in_8), .in_3(in_9), .in_4(1'b0), .in_5(1'b0), .in_6(in_1), .in_7(in_2), .in_8(in_3),
    .in_9(in_4), .in_10(in_5), .in_11(in_6), .out_15(pro_1_out_15), .out_16(pro_1_out_16),
    .out_17(pro_1_out_17), .out_18(pro_1_out_18), .out_19(pro_1_out_19), .out_20(pro_1_out_20),
    .out_12(pro_1_out_12), .out_13(pro_1_out_13), .out_14(pro_1_out_14));
  Display_de_7_Segmentos display_de_7_segmentos_3 (
    .in_1(in_3), .in_2(in_4), .in_3(in_5), .in_4(in_6), .out_5(display_de_7_segmentos_3_out_5),
    .out_6(display_de_7_segmentos_3_out_6), .out_7(display_de_7_segmentos_3_out_7),
    .out_8(display_de_7_segmentos_3_out_8), .out_9(display_de_7_segmentos_3_out_9),
    .out_10(display_de_7_segmentos_3_out_10), .out_11(display_de_7_segmentos_3_out_11));
  Display_Especial_de_0 display_especial_de_0_1 (
    .AA(d0_2_out_4), .a(1'b0), .b(pro_1_out_12), .c(pro_1_out_13), .d(pro_1_out_14),
    .x(display_especial_de_0_1_x), .y(display_especial_de_0_1_y), .z(display_especial_de_0_1_z),
    .u(display_especial_de_0_1_u), .v(display_especial_de_0_1_v), .w(display_especial_de_0_1_w),
    .s(display_especial_de_0_1_s));
  Display_Especial display_especial_1 (
    .AA(d0_1_out_4), .a(1'b0), .b(1'b0), .c(pro_1_out_15), .d(pro_1_out_16), .x(display_especial_1_x),
    .y(display_especial_1_y), .z(display_especial_1_z), .u(display_especial_1_u), .v(display_especial_1_v),
    .w(display_especial_1_w), .s(display_especial_1_s));
  _7_Segment_Display u_7_segment_display_4 (
    .g(display_especial_1_s), .f(display_especial_1_w), .a(display_especial_1_x), .b(display_especial_1_y),
    .e(display_especial_1_v), .d(display_especial_1_u), .c(display_especial_1_z));  // open: dp
  _7_Segment_Display u_7_segment_display_5 (
    .g(display_de_7_segmentos_4_out_11), .f(display_de_7_segmentos_4_out_10),
    .a(display_de_7_segmentos_4_out_5), .b(display_de_7_segmentos_4_out_6),
    .e(display_de_7_segmentos_4_out_9), .d(display_de_7_segmentos_4_out_8), .c(display_de_7_segmentos_4_out_7));  // open: dp
  _7_Segment_Display u_7_segment_display_6 (
    .g(display_especial_de_0_1_s), .f(display_especial_de_0_1_w), .a(display_especial_de_0_1_x),
    .b(display_especial_de_0_1_y), .e(display_especial_de_0_1_v), .d(display_especial_de_0_1_u),
    .c(display_especial_de_0_1_z));  // open: dp
  Display_de_7_Segmentos display_de_7_segmentos_4 (
    .in_1(pro_1_out_17), .in_2(pro_1_out_18), .in_3(pro_1_out_19), .in_4(pro_1_out_20),
    .out_5(display_de_7_segmentos_4_out_5), .out_6(display_de_7_segmentos_4_out_6),
    .out_7(display_de_7_segmentos_4_out_7), .out_8(display_de_7_segmentos_4_out_8),
    .out_9(display_de_7_segmentos_4_out_9), .out_10(display_de_7_segmentos_4_out_10),
    .out_11(display_de_7_segmentos_4_out_11));

  // Notes on the sheet:
  //   DIVIDENDO
  //   DIVISOR
  //   RESIDUO
  //   COCIENTE
endmodule

module Display_de_7_Segmentos (
  input  in_1,
  input  in_2,
  input  in_3,
  input  in_4,
  output out_5,
  output out_6,
  output out_7,
  output out_8,
  output out_9,
  output out_10,
  output out_11
);

  Segmento_A segmento_a_1 (.Entrada_A(in_1), .Entrada_B(in_2), .Entrada_C(in_3), .Entrada_D(in_4), .out_5(out_5));
  Segmento_B segmento_b_1 (.in_1(in_1), .in_2(in_2), .in_3(in_3), .in_4(in_4), .out_5(out_6));
  Segmento_F segmento_f_1 (.in_1(in_1), .in_2(in_2), .in_3(in_3), .in_4(in_4), .out_5(out_10));
  Segmento_C segmento_c_1 (.in_1(in_1), .in_2(in_2), .in_3(in_3), .in_4(in_4), .out_5(out_7));
  Segmento_G segmento_g_1 (.in_1(in_1), .in_2(in_2), .in_3(in_3), .in_4(in_4), .out_5(out_11));
  Segmento_D segmento_d_1 (.in_1(in_1), .in_2(in_2), .in_3(in_3), .in_4(in_4), .out_5(out_8));
  Segmento_E segmento_e_1 (.in_1(in_1), .in_2(in_2), .in_3(in_3), .in_4(in_4), .out_5(out_9));
endmodule

module Segmento_A (
  input  Entrada_A,
  input  Entrada_B,
  input  Entrada_C,
  input  Entrada_D,
  output out_5
);

  wire and_1_out, and_2_out, and_3_out, and_4_out, and_5_out, and_6_out, not_1_out, not_2_out, not_3_out,
       not_4_out;

  not not_1 (not_1_out, Entrada_A);
  not not_2 (not_2_out, Entrada_B);
  not not_3 (not_3_out, Entrada_C);
  not not_4 (not_4_out, Entrada_D);
  and and_1 (and_1_out, not_1_out, Entrada_B, Entrada_D);
  and and_2 (and_2_out, Entrada_A, not_2_out, not_3_out);
  and and_3 (and_3_out, not_2_out, not_4_out);
  and and_4 (and_4_out, not_1_out, Entrada_C);
  and and_5 (and_5_out, Entrada_B, Entrada_C);
  and and_6 (and_6_out, Entrada_A, not_4_out);
  or or_1 (out_5, and_1_out, and_2_out, and_3_out, and_4_out, and_5_out, and_6_out);

  // Notes on the sheet:
  //   Circuito del Segmento A
  //   Salida Segmento A
endmodule

module Segmento_B (
  input  in_1,
  input  in_2,
  input  in_3,
  input  in_4,
  output out_5
);

  wire and_1_out, and_2_out, and_3_out, and_4_out, and_5_out, not_1_out, not_2_out, not_3_out, not_4_out;

  not not_1 (not_1_out, in_1);
  not not_2 (not_2_out, in_2);
  not not_3 (not_3_out, in_3);
  not not_4 (not_4_out, in_4);
  and and_1 (and_1_out, not_1_out, not_3_out, not_4_out);
  and and_2 (and_2_out, not_1_out, in_3, in_4);
  and and_3 (and_3_out, in_1, not_3_out, in_4);
  and and_4 (and_4_out, not_2_out, not_3_out);
  and and_5 (and_5_out, not_2_out, not_4_out);
  or or_1 (out_5, and_1_out, and_2_out, and_3_out, and_4_out, and_5_out);
endmodule

module Segmento_C (
  input  in_1,
  input  in_2,
  input  in_3,
  input  in_4,
  output out_5
);

  wire and_1_out, and_2_out, and_3_out, and_4_out, and_5_out, not_1_out, not_2_out, not_3_out;

  not not_1 (not_1_out, in_1);
  not not_2 (not_2_out, in_2);
  not not_3 (not_3_out, in_3);
  // NOT_Gate not_4 has open pins: in=in_4, out=open
  and and_1 (and_1_out, not_2_out, not_3_out);
  and and_2 (and_2_out, not_2_out, in_4);
  and and_3 (and_3_out, not_3_out, in_4);
  and and_4 (and_4_out, not_1_out, in_2);
  and and_5 (and_5_out, in_1, not_2_out);
  or or_1 (out_5, and_1_out, and_2_out, and_3_out, and_4_out, and_5_out);
endmodule

module Segmento_D (
  input  in_1,
  input  in_2,
  input  in_3,
  input  in_4,
  output out_5
);

  wire and_1_out, and_2_out, and_3_out, and_4_out, and_5_out, not_1_out, not_2_out, not_3_out, not_4_out;

  not not_1 (not_1_out, in_1);
  not not_2 (not_2_out, in_2);
  not not_3 (not_3_out, in_3);
  not not_4 (not_4_out, in_4);
  and and_1 (and_1_out, not_2_out, not_3_out, not_4_out);
  and and_2 (and_2_out, not_2_out, in_3, in_4);
  and and_3 (and_3_out, not_1_out, in_3, not_4_out);
  and and_4 (and_4_out, in_2, not_3_out, in_4);
  and and_5 (and_5_out, in_1, in_2, not_4_out);
  or or_1 (out_5, and_1_out, and_2_out, and_3_out, and_4_out, and_5_out);
endmodule

module Segmento_E (
  input  in_1,
  input  in_2,
  input  in_3,
  input  in_4,
  output out_5
);

  wire and_1_out, and_2_out, and_3_out, and_4_out, not_2_out, not_4_out;

  // NOT_Gate not_1 has open pins: in=in_1, out=open
  not not_2 (not_2_out, in_2);
  // NOT_Gate not_3 has open pins: in=in_3, out=open
  not not_4 (not_4_out, in_4);
  and and_1 (and_1_out, not_2_out, not_4_out);
  and and_2 (and_2_out, in_3, not_4_out);
  and and_3 (and_3_out, in_1, in_2);
  and and_4 (and_4_out, in_1, in_3);
  or or_1 (out_5, and_1_out, and_2_out, and_3_out, and_4_out);
endmodule

module Segmento_F (
  input  in_1,
  input  in_2,
  input  in_3,
  input  in_4,
  output out_5
);

  wire and_1_out, and_2_out, and_3_out, and_4_out, and_5_out, not_1_out, not_2_out, not_3_out, not_4_out;

  not not_1 (not_1_out, in_1);
  not not_2 (not_2_out, in_2);
  not not_3 (not_3_out, in_3);
  not not_4 (not_4_out, in_4);
  and and_1 (and_1_out, not_1_out, in_2, not_3_out);
  and and_2 (and_2_out, not_3_out, not_4_out);
  and and_3 (and_3_out, in_2, not_4_out);
  and and_4 (and_4_out, in_1, in_3);
  and and_5 (and_5_out, in_1, not_2_out);
  or or_1 (out_5, and_1_out, and_2_out, and_3_out, and_4_out, and_5_out);
endmodule

module Segmento_G (
  input  in_1,
  input  in_2,
  input  in_3,
  input  in_4,
  output out_5
);

  wire and_1_out, and_2_out, and_3_out, and_4_out, and_5_out, not_1_out, not_2_out, not_3_out, not_4_out;

  not not_1 (not_1_out, in_1);
  not not_2 (not_2_out, in_2);
  not not_3 (not_3_out, in_3);
  not not_4 (not_4_out, in_4);
  and and_1 (and_1_out, not_1_out, in_2, not_4_out);
  and and_2 (and_2_out, in_2, not_3_out, in_4);
  and and_3 (and_3_out, not_2_out, in_3);
  and and_4 (and_4_out, in_1, in_3);
  and and_5 (and_5_out, in_1, not_2_out);
  or or_1 (out_5, and_1_out, and_2_out, and_3_out, and_4_out, and_5_out);
endmodule

module Suma_de_2 (
  input  in_1,
  input  in_2,
  output out_3,
  output out_4
);

  wire and_1_out, and_2_out, not_1_out, not_2_out;

  not not_1 (not_1_out, in_1);
  not not_2 (not_2_out, in_2);
  and and_1 (and_1_out, not_1_out, in_2);
  and and_2 (and_2_out, in_1, not_2_out);
  and and_3 (out_3, in_1, in_2);
  or or_1 (out_4, and_1_out, and_2_out);
endmodule

module Suma_de_3 (
  input  in_1,
  input  in_2,
  input  in_3,
  output out_4,
  output out_5
);

  wire and_1_out, and_2_out, and_3_out, and_4_out, and_5_out, and_6_out, and_7_out, not_1_out, not_2_out,
       not_3_out;

  not not_1 (not_1_out, in_1);
  not not_2 (not_2_out, in_2);
  not not_3 (not_3_out, in_3);
  and and_1 (and_1_out, in_1, in_2);
  and and_2 (and_2_out, in_1, in_3);
  and and_3 (and_3_out, in_2, in_3);
  and and_4 (and_4_out, in_1, not_2_out, not_3_out);
  and and_5 (and_5_out, in_1, in_2, in_3);
  and and_6 (and_6_out, not_1_out, in_2, not_3_out);
  and and_7 (and_7_out, not_1_out, not_2_out, in_3);
  or or_1 (out_5, and_4_out, and_5_out, and_6_out, and_7_out);
  or or_2 (out_4, and_1_out, and_2_out, and_3_out);
endmodule

module Resta_de_2 (
  input  in_1,
  input  in_2,
  output out_3,
  output out_4
);

  wire and_2_out, and_3_out, not_1_out, not_2_out;

  not not_1 (not_1_out, in_1);
  not not_2 (not_2_out, in_2);
  and and_1 (out_3, not_1_out, in_2);
  and and_2 (and_2_out, not_1_out, in_2);
  and and_3 (and_3_out, in_1, not_2_out);
  or or_1 (out_4, and_2_out, and_3_out);
endmodule

module Resta_de_3 (
  input  in_1,
  input  in_2,
  input  in_3,
  output out_4,
  output out_5
);

  wire and_1_out, and_2_out, and_3_out, and_4_out, and_5_out, and_6_out, and_7_out, not_1_out, not_2_out,
       not_3_out;

  not not_1 (not_1_out, in_1);
  not not_2 (not_2_out, in_2);
  not not_3 (not_3_out, in_3);
  and and_1 (and_1_out, in_1, not_2_out);
  and and_2 (and_2_out, in_1, in_3);
  and and_3 (and_3_out, not_2_out, in_3);
  and and_4 (and_4_out, in_1, not_2_out, not_3_out);
  and and_5 (and_5_out, not_1_out, not_2_out, in_3);
  and and_6 (and_6_out, in_1, in_2, in_3);
  and and_7 (and_7_out, not_1_out, in_2, not_3_out);
  or or_1 (out_4, and_1_out, and_2_out, and_3_out);
  or or_2 (out_5, and_4_out, and_5_out, and_6_out, and_7_out);
endmodule

module Cociente_de_6 (
  input  a,
  input  b,
  input  c,
  input  d,
  input  e,
  input  f,
  output x
);

  wire and_1_out, and_2_out, and_3_out, and_4_out, and_5_out, and_6_out, and_7_out, and_8_out, and_9_out,
       and_10_out, and_11_out, not_1_out, not_2_out, not_3_out, not_4_out, not_5_out, not_6_out, not_7_out,
       not_8_out, not_9_out, not_10_out, not_11_out, not_12_out, not_13_out, not_14_out;

  not not_1 (not_1_out, a);
  not not_2 (not_2_out, b);
  and and_1 (and_1_out, not_1_out, not_2_out, c, f);
  not not_3 (not_3_out, b);
  not not_4 (not_4_out, c);
  not not_5 (not_5_out, a);
  not not_6 (not_6_out, a);
  not not_7 (not_7_out, b);
  not not_8 (not_8_out, a);
  not not_9 (not_9_out, b);
  and and_2 (and_2_out, not_9_out, c, d, e);
  and and_3 (and_3_out, not_6_out, not_7_out, c, e);
  not not_10 (not_10_out, a);
  not not_11 (not_11_out, a);
  and and_4 (and_4_out, not_11_out, b, not_4_out, e);
  not not_12 (not_12_out, c);
  and and_5 (and_5_out, not_8_out, c, e, f);
  and and_6 (and_6_out, not_10_out, c, d);
  and and_7 (and_7_out, not_5_out, b, d);
  and and_8 (and_8_out, b, not_12_out, d, e);
  and and_9 (and_9_out, not_3_out, c, d, f);
  not not_13 (not_13_out, b);
  not not_14 (not_14_out, c);
  and and_10 (and_10_out, a, not_13_out, not_14_out, d);
  and and_11 (and_11_out, a, d, e, f);
  or or_1 (x, and_1_out, and_3_out, and_5_out, and_6_out, and_9_out, and_2_out, and_4_out, and_7_out, and_8_out, and_10_out, and_11_out);
endmodule

module MULTIPLICACION (
  input  in_1,
  input  in_2,
  input  in_3,
  input  in_4,
  output out_5,
  output out_6,
  output out_7
);

  and and_1 (out_5, in_1, in_4);
  and and_2 (out_6, in_2, in_4);
  and and_3 (out_7, in_3, in_4);
endmodule

module Pro (
  input  in_1,
  input  in_2,
  input  in_3,
  input  in_4,
  input  in_5,
  input  in_6,
  input  in_7,
  input  in_8,
  input  in_9,
  input  in_10,
  input  in_11,
  output out_12,
  output out_13,
  output out_14,
  output out_15,
  output out_16,
  output out_17,
  output out_18,
  output out_19,
  output out_20
);

  wire multiplicacion_1_out_5, multiplicacion_1_out_6, multiplicacion_1_out_7, multiplicacion_2_out_5,
       multiplicacion_2_out_6, multiplicacion_2_out_7, multiplicacion_3_out_5, multiplicacion_3_out_6,
       multiplicacion_3_out_7, multiplicacion_4_out_5, multiplicacion_4_out_6, multiplicacion_4_out_7,
       multiplicacion_5_out_5, multiplicacion_5_out_6, multiplicacion_5_out_7, multiplicacion_6_out_5,
       multiplicacion_6_out_6, multiplicacion_6_out_7, resta_de_2_1_out_3, resta_de_2_1_out_4,
       resta_de_2_2_out_3, resta_de_2_2_out_4, resta_de_2_3_out_3, resta_de_2_3_out_4, resta_de_2_4_out_3,
       resta_de_2_4_out_4, resta_de_2_5_out_3, resta_de_2_5_out_4, resta_de_2_6_out_3, resta_de_2_6_out_4,
       resta_de_2_7_out_3, resta_de_2_7_out_4, resta_de_2_8_out_3, resta_de_2_8_out_4, resta_de_2_9_out_3,
       resta_de_2_9_out_4, resta_de_2_10_out_3, resta_de_2_11_out_3, resta_de_2_11_out_4, resta_de_3_1_out_4,
       resta_de_3_1_out_5, resta_de_3_2_out_4, resta_de_3_2_out_5, resta_de_3_3_out_4, resta_de_3_3_out_5,
       resta_de_3_4_out_4, resta_de_3_4_out_5, resta_de_3_5_out_4, resta_de_3_5_out_5, resta_de_3_6_out_4,
       resta_de_3_6_out_5, resta_de_3_7_out_4, resta_de_3_7_out_5, resta_de_3_8_out_4, resta_de_3_8_out_5,
       resta_de_3_9_out_4, resta_de_3_9_out_5, resta_de_3_10_out_4, resta_de_3_10_out_5, resta_de_3_11_out_4,
       resta_de_3_12_out_4;

  // Cociente_de_6 cociente_de_6_1: pin names not known; wires that end beside it: in_1, in_2, in_3, in_4, in_5, in_6, out_15
  Resta_de_2 resta_de_2_1 (
    .in_1(in_6), .in_2(multiplicacion_1_out_7), .out_3(resta_de_2_1_out_3), .out_4(resta_de_2_1_out_4));
  MULTIPLICACION multiplicacion_1 (
    .in_1(in_1), .in_2(in_2), .in_3(in_3), .in_4(out_15), .out_5(multiplicacion_1_out_5),
    .out_6(multiplicacion_1_out_6), .out_7(multiplicacion_1_out_7));
  Resta_de_3 resta_de_3_1 (
    .in_1(resta_de_2_1_out_3), .in_2(in_5), .in_3(multiplicacion_1_out_6), .out_4(resta_de_3_1_out_4),
    .out_5(resta_de_3_1_out_5));
  Resta_de_3 resta_de_3_2 (
    .in_1(resta_de_3_1_out_4), .in_2(in_4), .in_3(multiplicacion_1_out_5), .out_4(resta_de_3_2_out_4),
    .out_5(resta_de_3_2_out_5));
  Cociente_de_7 cociente_de_7_1 (
    .a(in_1), .b(in_2), .c(in_3), .d(resta_de_3_2_out_5), .e(resta_de_3_1_out_5), .f(resta_de_2_1_out_4),
    .g(in_7), .x(out_16));
  MULTIPLICACION multiplicacion_2 (
    .in_1(in_1), .in_2(in_2), .in_3(in_3), .in_4(out_16), .out_5(multiplicacion_2_out_5),
    .out_6(multiplicacion_2_out_6), .out_7(multiplicacion_2_out_7));
  Resta_de_2 resta_de_2_2 (
    .in_1(in_7), .in_2(multiplicacion_2_out_7), .out_3(resta_de_2_2_out_3), .out_4(resta_de_2_2_out_4));
  Resta_de_3 resta_de_3_3 (
    .in_1(resta_de_2_2_out_3), .in_2(resta_de_2_1_out_4), .in_3(multiplicacion_2_out_6),
    .out_4(resta_de_3_3_out_4), .out_5(resta_de_3_3_out_5));
  Resta_de_3 resta_de_3_4 (
    .in_1(resta_de_3_3_out_4), .in_2(resta_de_3_1_out_5), .in_3(multiplicacion_2_out_5),
    .out_4(resta_de_3_4_out_4), .out_5(resta_de_3_4_out_5));
  Resta_de_2 resta_de_2_3 (
    .in_1(resta_de_3_4_out_4), .in_2(resta_de_3_2_out_5), .out_3(resta_de_2_3_out_3),
    .out_4(resta_de_2_3_out_4));
  Cociente_de_7 cociente_de_7_2 (
    .a(in_1), .b(in_2), .c(in_3), .d(resta_de_3_4_out_5), .e(resta_de_3_3_out_5), .f(resta_de_2_2_out_4),
    .g(in_8), .x(out_17));
  MULTIPLICACION multiplicacion_3 (
    .in_1(in_1), .in_2(in_2), .in_3(in_3), .in_4(out_17), .out_5(multiplicacion_3_out_5),
    .out_6(multiplicacion_3_out_6), .out_7(multiplicacion_3_out_7));
  Resta_de_2 resta_de_2_4 (
    .in_1(in_8), .in_2(multiplicacion_3_out_7), .out_3(resta_de_2_4_out_3), .out_4(resta_de_2_4_out_4));
  Resta_de_3 resta_de_3_5 (
    .in_1(resta_de_2_4_out_3), .in_2(resta_de_2_2_out_4), .in_3(multiplicacion_3_out_6),
    .out_4(resta_de_3_5_out_4), .out_5(resta_de_3_5_out_5));
  Resta_de_3 resta_de_3_6 (
    .in_1(resta_de_3_5_out_4), .in_2(resta_de_3_3_out_5), .in_3(multiplicacion_3_out_5),
    .out_4(resta_de_3_6_out_4), .out_5(resta_de_3_6_out_5));
  Resta_de_2 resta_de_2_5 (
    .in_1(resta_de_3_6_out_4), .in_2(resta_de_3_4_out_5), .out_3(resta_de_2_5_out_3),
    .out_4(resta_de_2_5_out_4));
  Cociente_de_7 cociente_de_7_3 (
    .a(in_1), .b(in_2), .c(in_3), .d(resta_de_3_6_out_5), .e(resta_de_3_5_out_5), .f(resta_de_2_4_out_4),
    .g(in_9), .x(out_18));
  MULTIPLICACION multiplicacion_4 (
    .in_1(in_1), .in_2(in_2), .in_3(in_3), .in_4(out_18), .out_5(multiplicacion_4_out_5),
    .out_6(multiplicacion_4_out_6), .out_7(multiplicacion_4_out_7));
  Resta_de_2 resta_de_2_6 (
    .in_1(in_9), .in_2(multiplicacion_4_out_7), .out_3(resta_de_2_6_out_3), .out_4(resta_de_2_6_out_4));
  Resta_de_3 resta_de_3_7 (
    .in_1(resta_de_2_6_out_3), .in_2(resta_de_2_4_out_4), .in_3(multiplicacion_4_out_6),
    .out_4(resta_de_3_7_out_4), .out_5(resta_de_3_7_out_5));
  Resta_de_3 resta_de_3_8 (
    .in_1(resta_de_3_7_out_4), .in_2(resta_de_3_5_out_5), .in_3(multiplicacion_4_out_5),
    .out_4(resta_de_3_8_out_4), .out_5(resta_de_3_8_out_5));
  Resta_de_2 resta_de_2_7 (
    .in_1(resta_de_3_8_out_4), .in_2(resta_de_3_6_out_5), .out_3(resta_de_2_7_out_3),
    .out_4(resta_de_2_7_out_4));
  Cociente_de_7 cociente_de_7_4 (
    .a(in_1), .b(in_2), .c(in_3), .d(resta_de_3_8_out_5), .e(resta_de_3_7_out_5), .f(resta_de_2_6_out_4),
    .g(in_10), .x(out_19));
  MULTIPLICACION multiplicacion_5 (
    .in_1(in_1), .in_2(in_2), .in_3(in_3), .in_4(out_19), .out_5(multiplicacion_5_out_5),
    .out_6(multiplicacion_5_out_6), .out_7(multiplicacion_5_out_7));
  Resta_de_2 resta_de_2_8 (
    .in_1(in_10), .in_2(multiplicacion_5_out_7), .out_3(resta_de_2_8_out_3), .out_4(resta_de_2_8_out_4));
  Resta_de_3 resta_de_3_9 (
    .in_1(resta_de_2_8_out_3), .in_2(resta_de_2_6_out_4), .in_3(multiplicacion_5_out_6),
    .out_4(resta_de_3_9_out_4), .out_5(resta_de_3_9_out_5));
  Resta_de_3 resta_de_3_10 (
    .in_1(resta_de_3_9_out_4), .in_2(resta_de_3_7_out_5), .in_3(multiplicacion_5_out_5),
    .out_4(resta_de_3_10_out_4), .out_5(resta_de_3_10_out_5));
  Resta_de_2 resta_de_2_9 (
    .in_1(resta_de_3_10_out_4), .in_2(resta_de_3_8_out_5), .out_3(resta_de_2_9_out_3),
    .out_4(resta_de_2_9_out_4));
  Cociente_de_7 cociente_de_7_5 (
    .a(in_1), .b(in_2), .c(in_3), .d(resta_de_3_10_out_5), .e(resta_de_3_9_out_5), .f(resta_de_2_8_out_4),
    .g(in_11), .x(out_20));
  MULTIPLICACION multiplicacion_6 (
    .in_1(in_1), .in_2(in_2), .in_3(in_3), .in_4(out_20), .out_5(multiplicacion_6_out_5),
    .out_6(multiplicacion_6_out_6), .out_7(multiplicacion_6_out_7));
  Resta_de_2 resta_de_2_10 (.in_1(in_11), .in_2(multiplicacion_6_out_7), .out_3(resta_de_2_10_out_3), .out_4(out_14));
  Resta_de_3 resta_de_3_11 (
    .in_1(resta_de_2_10_out_3), .in_2(resta_de_2_8_out_4), .in_3(multiplicacion_6_out_6),
    .out_4(resta_de_3_11_out_4), .out_5(out_13));
  Resta_de_3 resta_de_3_12 (
    .in_1(resta_de_3_11_out_4), .in_2(resta_de_3_9_out_5), .in_3(multiplicacion_6_out_5),
    .out_4(resta_de_3_12_out_4), .out_5(out_12));
  Resta_de_2 resta_de_2_11 (
    .in_1(resta_de_3_12_out_4), .in_2(resta_de_3_10_out_5), .out_3(resta_de_2_11_out_3),
    .out_4(resta_de_2_11_out_4));
  // also tied to GND on the sheet: {resta_de_3_2_out_4, resta_de_2_3_out_3, resta_de_2_3_out_4, resta_de_2_5_out_3, resta_de_2_5_out_4, resta_de_2_7_out_3, resta_de_2_7_out_4, resta_de_2_9_out_3, resta_de_2_9_out_4, resta_de_2_11_out_3, resta_de_2_11_out_4}
endmodule

module Cociente_de_7 (
  input  a,
  input  b,
  input  c,
  input  d,
  input  e,
  input  f,
  input  g,
  output x
);

  wire and_1_out, and_2_out, and_3_out, and_4_out, and_5_out, and_6_out, and_7_out, and_8_out, and_9_out,
       and_10_out, and_11_out, and_12_out, and_13_out, and_14_out, not_1_out, not_2_out, not_3_out,
       not_4_out, not_5_out, not_6_out, not_7_out, not_8_out, not_9_out, not_10_out, not_11_out, not_12_out,
       not_13_out, not_14_out;

  not not_1 (not_1_out, a);
  not not_2 (not_2_out, b);
  not not_3 (not_3_out, a);
  not not_4 (not_4_out, b);
  not not_5 (not_5_out, a);
  not not_6 (not_6_out, a);
  not not_7 (not_7_out, b);
  not not_8 (not_8_out, b);
  not not_9 (not_9_out, a);
  not not_10 (not_10_out, c);
  not not_11 (not_11_out, a);
  not not_12 (not_12_out, c);
  not not_13 (not_13_out, b);
  not not_14 (not_14_out, c);
  and and_1 (and_1_out, not_1_out, not_2_out, c, g);
  and and_2 (and_2_out, not_3_out, not_4_out, c, f);
  and and_3 (and_3_out, not_5_out, c, f, g);
  and and_4 (and_4_out, not_6_out, c, e);
  and and_5 (and_5_out, not_7_out, c, e, g);
  and and_6 (and_6_out, not_8_out, c, e, f);
  and and_7 (and_7_out, c, d);
  and and_8 (and_8_out, not_9_out, b, not_10_out, f);
  and and_9 (and_9_out, not_11_out, b, e);
  and and_10 (and_10_out, b, not_12_out, e, f);
  and and_11 (and_11_out, b, d);
  and and_12 (and_12_out, a, not_13_out, not_14_out, e);
  and and_13 (and_13_out, a, e, f, g);
  and and_14 (and_14_out, a, d);
  or or_1 (x, and_1_out, and_2_out, and_3_out, and_4_out, and_5_out, and_6_out, and_7_out, and_8_out, and_9_out, and_10_out, and_11_out, and_12_out, and_13_out, and_14_out);
endmodule

module D0 (
  input  in_1,
  input  in_2,
  input  in_3,
  output out_4
);

  or or_1 (out_4, in_1, in_2, in_3);
endmodule

module Display_Especial (
  input  AA,
  input  a,
  input  b,
  input  c,
  input  d,
  output x,
  output y,
  output z,
  output u,
  output v,
  output w,
  output s
);

  wire and_1_out, and_2_out, and_3_out, and_4_out, and_5_out, and_6_out, and_7_out, and_8_out, and_9_out,
       and_10_out, and_11_out, and_12_out, and_13_out, and_14_out, and_15_out, and_16_out, and_17_out,
       and_18_out, and_19_out, and_20_out, and_21_out, and_22_out, and_23_out, and_24_out, and_25_out,
       and_26_out, and_27_out, and_28_out, and_29_out, and_30_out, and_31_out, and_32_out, and_33_out,
       and_34_out, and_35_out, not_1_out, not_2_out, not_3_out, not_4_out, not_5_out, not_6_out, not_7_out,
       not_8_out, not_9_out, not_10_out, not_11_out, not_12_out, not_13_out, not_14_out, not_15_out,
       not_16_out, not_17_out, not_18_out, not_19_out, not_20_out, not_21_out, not_22_out, not_23_out,
       not_24_out, not_25_out, not_26_out, not_27_out, not_28_out, not_29_out, not_30_out, not_31_out,
       not_32_out, not_33_out, not_34_out, not_35_out, not_36_out, not_37_out, not_38_out, not_39_out,
       not_40_out, not_41_out, not_42_out, not_43_out, not_44_out, not_45_out, not_46_out, not_47_out,
       not_48_out, not_49_out;

  not not_1 (not_1_out, b);
  not not_2 (not_2_out, d);
  not not_3 (not_3_out, a);
  not not_4 (not_4_out, a);
  not not_5 (not_5_out, b);
  not not_6 (not_6_out, c);
  not not_7 (not_7_out, d);
  not not_8 (not_8_out, a);
  not not_9 (not_9_out, b);
  not not_10 (not_10_out, a);
  not not_11 (not_11_out, c);
  not not_12 (not_12_out, d);
  not not_13 (not_13_out, b);
  not not_14 (not_14_out, d);
  not not_15 (not_15_out, a);
  not not_16 (not_16_out, c);
  not not_17 (not_17_out, a);
  not not_18 (not_18_out, c);
  not not_19 (not_19_out, a);
  not not_20 (not_20_out, c);
  not not_21 (not_21_out, a);
  not not_22 (not_22_out, b);
  not not_23 (not_23_out, a);
  not not_24 (not_24_out, b);
  not not_25 (not_25_out, d);
  not not_26 (not_26_out, b);
  not not_27 (not_27_out, c);
  not not_28 (not_28_out, d);
  not not_29 (not_29_out, c);
  not not_30 (not_30_out, d);
  not not_31 (not_31_out, b);
  not not_32 (not_32_out, d);
  not not_33 (not_33_out, d);
  not not_34 (not_34_out, c);
  not not_35 (not_35_out, d);
  not not_36 (not_36_out, a);
  not not_37 (not_37_out, c);
  not not_38 (not_38_out, d);
  not not_39 (not_39_out, b);
  not not_40 (not_40_out, b);
  not not_41 (not_41_out, d);
  not not_42 (not_42_out, a);
  not not_43 (not_43_out, c);
  not not_44 (not_44_out, b);
  and and_1 (and_1_out, AA, not_1_out, not_2_out);
  and and_2 (and_2_out, AA, not_3_out, c);
  and and_3 (and_3_out, AA, not_4_out, b, d);
  and and_4 (and_4_out, AA, b, c);
  and and_5 (and_5_out, AA, a, not_5_out, not_6_out);
  and and_6 (and_6_out, AA, a, not_7_out);
  not not_45 (not_45_out, AA);
  and and_7 (and_7_out, not_8_out, not_9_out);
  and and_8 (and_8_out, not_10_out, not_11_out, not_12_out);
  and and_9 (and_9_out, not_13_out, not_14_out);
  and and_10 (and_10_out, not_15_out, c, d);
  and and_11 (and_11_out, a, not_16_out, d);
  not not_46 (not_46_out, AA);
  and and_12 (and_12_out, not_17_out, not_18_out);
  and and_13 (and_13_out, not_19_out, d);
  and and_14 (and_14_out, not_20_out, d);
  and and_15 (and_15_out, not_21_out, b);
  and and_16 (and_16_out, a, not_22_out);
  not not_47 (not_47_out, AA);
  and and_17 (and_17_out, not_23_out, not_24_out, not_25_out);
  and and_18 (and_18_out, not_26_out, c, d);
  and and_19 (and_19_out, b, not_27_out, d);
  and and_20 (and_20_out, b, c, not_28_out);
  and and_21 (and_21_out, a, not_29_out, not_30_out);
  not not_48 (not_48_out, AA);
  and and_22 (and_22_out, not_31_out, not_32_out);
  and and_23 (and_23_out, c, not_33_out);
  and and_24 (and_24_out, a, c);
  and and_25 (and_25_out, a, b);
  and and_26 (and_26_out, AA, not_34_out, not_35_out);
  and and_27 (and_27_out, AA, not_36_out, b, not_37_out);
  and and_28 (and_28_out, AA, b, not_38_out);
  and and_29 (and_29_out, AA, a, not_39_out);
  and and_30 (and_30_out, AA, a, c);
  not not_49 (not_49_out, AA);
  and and_31 (and_31_out, not_40_out, c);
  and and_32 (and_32_out, c, not_41_out);
  and and_33 (and_33_out, not_42_out, b, not_43_out);
  and and_34 (and_34_out, a, not_44_out);
  and and_35 (and_35_out, a, d);
  or or_1 (x, and_1_out, and_2_out, and_3_out, and_4_out, and_5_out, and_6_out);
  or or_2 (y, not_45_out, and_7_out, and_8_out, and_9_out, and_10_out, and_11_out);
  or or_3 (z, not_46_out, and_12_out, and_13_out, and_14_out, and_15_out, and_16_out);
  or or_4 (u, not_47_out, and_17_out, and_18_out, and_19_out, and_20_out, and_21_out);
  or or_5 (v, not_48_out, and_22_out, and_23_out, and_24_out, and_25_out);
  or or_6 (w, and_26_out, and_27_out, and_28_out, and_29_out, and_30_out);
  or or_7 (s, not_49_out, and_31_out, and_32_out, and_33_out, and_34_out, and_35_out);
endmodule

module Display_Especial_de_0 (
  input  AA,
  input  a,
  input  b,
  input  c,
  input  d,
  output x,
  output y,
  output z,
  output u,
  output v,
  output w,
  output s
);

  wire and_1_out, and_2_out, and_3_out, and_4_out, and_5_out, and_6_out, and_7_out, and_8_out, and_9_out,
       and_10_out, and_11_out, and_12_out, and_13_out, and_14_out, and_15_out, and_16_out, and_17_out,
       and_18_out, and_19_out, and_20_out, and_21_out, and_22_out, and_23_out, and_24_out, and_25_out,
       and_26_out, and_27_out, and_28_out, and_29_out, and_30_out, and_31_out, and_32_out, and_33_out,
       and_34_out, and_35_out, and_36_out, not_1_out, not_2_out, not_3_out, not_4_out, not_5_out, not_6_out,
       not_7_out, not_8_out, not_9_out, not_10_out, not_11_out, not_12_out, not_13_out, not_14_out,
       not_15_out, not_16_out, not_17_out, not_18_out, not_19_out, not_20_out, not_21_out, not_22_out,
       not_23_out, not_24_out, not_25_out, not_26_out, not_27_out, not_28_out, not_29_out, not_30_out,
       not_31_out, not_32_out, not_33_out, not_34_out, not_35_out, not_36_out, not_37_out, not_38_out,
       not_39_out, not_40_out, not_41_out, not_42_out, not_43_out, not_44_out, not_45_out, not_46_out,
       not_47_out, not_48_out, not_49_out, not_50_out;

  not not_1 (not_1_out, b);
  not not_2 (not_2_out, d);
  not not_3 (not_3_out, a);
  not not_4 (not_4_out, a);
  not not_5 (not_5_out, b);
  not not_6 (not_6_out, c);
  not not_7 (not_7_out, d);
  not not_8 (not_8_out, a);
  not not_9 (not_9_out, b);
  not not_10 (not_10_out, a);
  not not_11 (not_11_out, c);
  not not_12 (not_12_out, d);
  not not_13 (not_13_out, b);
  not not_14 (not_14_out, d);
  not not_15 (not_15_out, a);
  not not_16 (not_16_out, c);
  not not_17 (not_17_out, a);
  not not_18 (not_18_out, c);
  not not_19 (not_19_out, a);
  not not_20 (not_20_out, c);
  not not_21 (not_21_out, a);
  not not_22 (not_22_out, b);
  not not_23 (not_23_out, a);
  not not_24 (not_24_out, b);
  not not_25 (not_25_out, d);
  not not_26 (not_26_out, b);
  not not_27 (not_27_out, c);
  not not_28 (not_28_out, d);
  not not_29 (not_29_out, c);
  not not_30 (not_30_out, d);
  not not_31 (not_31_out, b);
  not not_32 (not_32_out, d);
  not not_33 (not_33_out, d);
  not not_34 (not_34_out, c);
  not not_35 (not_35_out, d);
  not not_36 (not_36_out, a);
  not not_37 (not_37_out, c);
  not not_38 (not_38_out, d);
  not not_39 (not_39_out, b);
  not not_40 (not_40_out, b);
  not not_41 (not_41_out, d);
  not not_42 (not_42_out, a);
  not not_43 (not_43_out, c);
  not not_44 (not_44_out, b);
  not not_45 (not_45_out, AA);
  and and_1 (and_1_out, not_1_out, not_2_out);
  and and_2 (and_2_out, not_3_out, c);
  and and_3 (and_3_out, not_4_out, b, d);
  and and_4 (and_4_out, b, c);
  and and_5 (and_5_out, a, not_5_out, not_6_out);
  and and_6 (and_6_out, a, not_7_out);
  not not_46 (not_46_out, AA);
  and and_7 (and_7_out, not_8_out, not_9_out);
  and and_8 (and_8_out, not_10_out, not_11_out, not_12_out);
  and and_9 (and_9_out, not_13_out, not_14_out);
  and and_10 (and_10_out, not_15_out, c, d);
  and and_11 (and_11_out, a, not_16_out, d);
  not not_47 (not_47_out, AA);
  and and_12 (and_12_out, not_17_out, not_18_out);
  and and_13 (and_13_out, not_19_out, d);
  and and_14 (and_14_out, not_20_out, d);
  and and_15 (and_15_out, not_21_out, b);
  and and_16 (and_16_out, a, not_22_out);
  not not_48 (not_48_out, AA);
  and and_17 (and_17_out, not_23_out, not_24_out, not_25_out);
  and and_18 (and_18_out, not_26_out, c, d);
  and and_19 (and_19_out, b, not_27_out, d);
  and and_20 (and_20_out, b, c, not_28_out);
  and and_21 (and_21_out, a, not_29_out, not_30_out);
  not not_49 (not_49_out, AA);
  and and_22 (and_22_out, not_31_out, not_32_out);
  and and_23 (and_23_out, c, not_33_out);
  and and_24 (and_24_out, a, c);
  and and_25 (and_25_out, a, b);
  not not_50 (not_50_out, AA);
  and and_26 (and_26_out, not_34_out, not_35_out);
  and and_27 (and_27_out, not_36_out, b, not_37_out);
  and and_28 (and_28_out, b, not_38_out);
  and and_29 (and_29_out, a, not_39_out);
  and and_30 (and_30_out, a, c);
  and and_31 (and_31_out, AA, not_40_out, c);
  and and_32 (and_32_out, AA, c, not_41_out);
  and and_33 (and_33_out, AA, not_42_out, b, not_43_out);
  and and_34 (and_34_out, AA, a, not_44_out);
  and and_35 (and_35_out, AA, a, d);
  and and_36 (and_36_out, AA, a, c);
  or or_1 (x, not_45_out, and_1_out, and_2_out, and_3_out, and_4_out, and_5_out, and_6_out);
  or or_2 (y, not_46_out, and_7_out, and_8_out, and_9_out, and_10_out, and_11_out);
  or or_3 (z, not_47_out, and_12_out, and_13_out, and_14_out, and_15_out, and_16_out);
  or or_4 (u, not_48_out, and_17_out, and_18_out, and_19_out, and_20_out, and_21_out);
  or or_5 (v, not_49_out, and_22_out, and_23_out, and_24_out, and_25_out);
  or or_6 (w, not_50_out, and_26_out, and_27_out, and_28_out, and_29_out, and_30_out);
  or or_7 (s, and_31_out, and_32_out, and_33_out, and_34_out, and_35_out, and_36_out);
endmodule
